// Logisim project ALU.circ as structural Verilog: 8 circuits, main circuit ALU
module ALU (
  input  [3:0] Selector,
  input  [31:0] In1,
  input  [31:0] In2,
  input  in_4,
  output Carry,
  output [31:0] Output,
  output ZF,
  output [31:0] Remainder,
  output SF
);

  wire _1_t, _2_t, C, C_t, not_1_out, os;
  wire [31:0] AND, Carry_DIVU, Carry_MULU, Carry_t, Carry_X, DIVU, multiplexer_1_out, multiplexer_2_out,
       multiplexer_3_out, multiplexer_4_out, multiplexer_5_out, multiplexer_8_out, multiplexer_9_out, MULU,
       negator_1_out, negator_2_out, negator_3_out, negator_4_out, negator_5_out, negator_6_out, NOR, OR,
       Out, Out_minus, Out_plus, Out_star, single_bit_negator_1_out_2, SLT, SLTU, XOR;

  DIVU divu_1 (.in_2(In1), .in_3(In2), .Output(DIVU), .Remainder(Carry_DIVU), .in_1(in_4));
  and and_1 (_1_t, In1[31], in_4);
  and and_2 (_2_t, in_4, In2[31]);
  Adder #(.width(32)) adder_1 (.a(In1), .b(In2), .out(Out_plus), .cin(1'b0), .cout(C));
  Subtractor #(.width(32)) subtractor_1 (.a(In1), .b(In2), .out(Out_minus), .bin(1'b0), .bout(C_t));
  MULU mulu_1 (.in_2(In1), .in_3(In2), .Output(MULU), .Carry_Out(Carry_MULU), .in_1(in_4));
  Negator #(.width(32)) negator_1 (.in(In1), .out(negator_1_out));
  Negator #(.width(32)) negator_2 (.in(In2), .out(negator_2_out));
  SLT slt_1 (.in_1(In1), .in_2(In2), .out_3(SLT));
  SLTU sltu_1 (.in_1(In1), .in_2(In2), .Output(SLTU));
  Multiplexer #(.width(32), .enable("false")) multiplexer_1 (
    .in0(In1), .in1(negator_1_out), .out(multiplexer_1_out), .sel(_1_t));
  Multiplexer #(.width(32), .enable("false")) multiplexer_2 (
    .in0(In2), .in1(negator_2_out), .out(multiplexer_2_out), .sel(_2_t));
  assign AND = In1 & In2;  // AND_Gate and_3, 32 bits wide
  assign NOR = ~(In1 | In2);  // NOR_Gate nor_1, 32 bits wide
  assign OR = In1 | In2;  // OR_Gate or_1, 32 bits wide
  assign XOR = In1 ^ In2;  // XOR_Gate xor_1, 32 bits wide
  Multiplier #(.width(32)) multiplier_1 (
    .a(multiplexer_1_out), .b(multiplexer_2_out), .out(Out_star), .cout(Carry_X));  // open: cin
  Negator #(.width(32)) negator_3 (.in(Out_star), .out(negator_3_out));
  Negator #(.width(32)) negator_4 (.in(Out), .out(negator_4_out));
  Single_bit_negator single_bit_negator_1 (.in_1(SLT), .out_2(single_bit_negator_1_out_2));
  Multiplexer #(.width(32), .enable("false")) multiplexer_3 (
    .in0(Out_star), .in1(negator_3_out), .out(multiplexer_3_out), .sel(os));
  Multiplexer #(.width(32), .enable("false")) multiplexer_4 (
    .in0(Out), .in1(negator_4_out), .out(multiplexer_4_out), .sel(os));
  Multiplexer #(.width(32), .enable("false")) multiplexer_5 (
    .in0(SLT), .in1(single_bit_negator_1_out_2), .out(multiplexer_5_out), .sel(not_1_out));
  not not_1 (not_1_out, os);
  Multiplexer #(.select(4), .width(32), .enable("false")) multiplexer_6 (
    .in2(Carry_X), .in3(Carry_t), .in9(Carry_MULU), .in10(Carry_DIVU), .out(Remainder), .sel(Selector));  // open: in0, in1, in4, in5, in6, in7, in8, in11, in12, in13, in14, in15
  xor xor_2 (os, _1_t, _2_t);
  Negator #(.width(32)) negator_5 (.in(In1), .out(negator_5_out));
  Negator #(.width(32)) negator_6 (.in(In2), .out(negator_6_out));
  Multiplexer #(.select(4), .width(32), .enable("false")) multiplexer_7 (
    .in0(Out_plus), .in1(Out_minus), .in2(multiplexer_3_out), .in3(multiplexer_4_out), .in4(AND), .in5(NOR),
    .in6(OR), .in7(XOR), .in8(multiplexer_5_out), .in9(Out_star), .in10(Out),
    .in11(single_bit_negator_1_out_2), .out(Output), .sel(Selector));  // open: in12, in13, in14, in15
  Multiplexer #(.width(32), .enable("false")) multiplexer_8 (
    .in0(In1), .in1(negator_5_out), .out(multiplexer_8_out), .sel(_1_t));
  Multiplexer #(.width(32), .enable("false")) multiplexer_9 (
    .in0(In2), .in1(negator_6_out), .out(multiplexer_9_out), .sel(_2_t));
  Divider #(.width(32)) divider_1 (
    .a(multiplexer_8_out), .b(multiplexer_9_out), .out(Out), .rem(Carry_t));  // open: upper
  Multiplexer #(.select(4)) multiplexer_10 (
    .in0(C), .in1(C_t), .in2(1'b0), .in3(1'b0), .in4(1'b0), .in5(1'b0), .in6(1'b0), .in7(1'b0), .in8(1'b0),
    .in9(1'b0), .out(Carry), .sel(Selector));  // open: in10, in11, in12, in13, in14, in15, en
  ZF zf_1 (.in_1(Output), .out_2(ZF));
  SF sf_1 (.in_1(Output), .out_2(SF));

  // Other names for the same wires on the sheet: _1[31:0] = In1; bit_31__1 = In1[31]; _2[31:0] = In2;
  //   bit_31__2 = In2[31]; Sign = in_4
endmodule

module SLT (
  input  [31:0] in_1,
  input  [31:0] in_2,
  output [31:0] out_3
);

  wire comparator_1_lt;

  Comparator #(.width(32)) comparator_1 (.a(in_1), .b(in_2), .lt(comparator_1_lt));  // open: gt, eq
  Multiplexer #(.width(32), .enable("false")) multiplexer_1 (
    .in0({32{1'b0}}), .in1(32'h1), .out(out_3), .sel(comparator_1_lt));
endmodule

module ZF (
  input  [31:0] in_1,
  output out_2
);

  wire or_1_out;

  or or_1 (or_1_out, in_1[0], in_1[1], in_1[2], in_1[3], in_1[4], in_1[5], in_1[6], in_1[7], in_1[8], in_1[9], in_1[10], in_1[11], in_1[12], in_1[13], in_1[14], in_1[15], in_1[16], in_1[17], in_1[18], in_1[19], in_1[20], in_1[21], in_1[22], in_1[23], in_1[24], in_1[25], in_1[26], in_1[27], in_1[28], in_1[29], in_1[30], in_1[31]);
  not not_1 (out_2, or_1_out);
endmodule

module SF (
  input  [31:0] in_1,
  output out_2
);

  Comparator #(.width(32)) comparator_1 (.a(in_1), .b({32{1'b0}}), .lt(out_2));  // open: gt, eq
endmodule

module MULU (
  input  in_1,
  input  [31:0] in_2,
  input  [31:0] in_3,
  output [31:0] Output,
  output [31:0] Carry_Out
);

  wire Out_1, Out_2;
  wire [31:0] IN_1_t, IN_2_t, negator_1_out, negator_2_out;

  and and_1 (Out_1, in_2[31], in_1);
  and and_2 (Out_2, in_1, in_3[31]);
  Negator #(.width(32)) negator_1 (.in(in_2), .out(negator_1_out));
  Negator #(.width(32)) negator_2 (.in(in_3), .out(negator_2_out));
  Multiplier #(.width(32)) multiplier_1 (.a(IN_1_t), .b(IN_2_t), .out(Output), .cout(Carry_Out));  // open: cin
  Multiplexer #(.width(32), .enable("false")) multiplexer_1 (
    .in0(in_2), .in1(negator_1_out), .out(IN_1_t), .sel(Out_1));
  Multiplexer #(.width(32), .enable("false")) multiplexer_2 (
    .in0(in_3), .in1(negator_2_out), .out(IN_2_t), .sel(Out_2));

  // Other names for the same wires on the sheet: _1[31:0] = in_2; bit_31__1 = in_2[31]; _2[31:0] = in_3;
  //   bit_31__2 = in_3[31]; Sign = in_1
endmodule

module DIVU (
  input  in_1,
  input  [31:0] in_2,
  input  [31:0] in_3,
  output [31:0] Output,
  output [31:0] Remainder
);

  wire Out_1, Out_2;
  wire [31:0] IN_1_t, IN_2_t, negator_1_out, negator_2_out;

  and and_1 (Out_1, in_2[31], in_1);
  and and_2 (Out_2, in_1, in_3[31]);
  Negator #(.width(32)) negator_1 (.in(in_2), .out(negator_1_out));
  Negator #(.width(32)) negator_2 (.in(in_3), .out(negator_2_out));
  Divider #(.width(32)) divider_1 (.a(IN_1_t), .b(IN_2_t), .out(Output), .rem(Remainder));  // open: upper
  Multiplexer #(.width(32), .enable("false")) multiplexer_1 (
    .in0(in_2), .in1(negator_1_out), .out(IN_1_t), .sel(Out_1));
  Multiplexer #(.width(32), .enable("false")) multiplexer_2 (
    .in0(in_3), .in1(negator_2_out), .out(IN_2_t), .sel(Out_2));

  // Other names for the same wires on the sheet: _1[31:0] = in_2; bit_31__1 = in_2[31]; _2[31:0] = in_3;
  //   bit_31__2 = in_3[31]; Sign = in_1
endmodule

module SLTU (
  input  [31:0] in_1,
  input  [31:0] in_2,
  output [31:0] Output
);

  wire Out_1, Out_2;
  wire [31:0] IN_1_t, IN_2_t, negator_1_out, negator_2_out;

  and and_1 (Out_1, in_1[31], 1'b1);
  and and_2 (Out_2, in_2[31], 1'b1);
  Negator #(.width(32)) negator_1 (.in(in_1), .out(negator_1_out));
  Negator #(.width(32)) negator_2 (.in(in_2), .out(negator_2_out));
  SLT slt_1 (.in_1(IN_1_t), .in_2(IN_2_t), .out_3(Output));
  Multiplexer #(.width(32), .enable("false")) multiplexer_1 (
    .in0(in_1), .in1(negator_1_out), .out(IN_1_t), .sel(Out_1));
  Multiplexer #(.width(32), .enable("false")) multiplexer_2 (
    .in0(in_2), .in1(negator_2_out), .out(IN_2_t), .sel(Out_2));

  // Other names for the same wires on the sheet: _1[31:0] = in_1; bit_31__1 = in_1[31]; _2[31:0] = in_2;
  //   bit_31__2 = in_2[31]
endmodule

module Single_bit_negator (
  input  [31:0] in_1,
  output [31:0] out_2
);

  wire comparator_1_eq;

  Comparator #(.width(32)) comparator_1 (.a(in_1), .b({32{1'b0}}), .eq(comparator_1_eq));  // open: gt, lt
  Multiplexer #(.width(32), .enable("false")) multiplexer_1 (
    .in0({32{1'b0}}), .in1(32'h1), .out(out_2), .sel(comparator_1_eq));
endmodule
