// Logisim project Branch Control.circ as structural Verilog: 1 circuit, main circuit Branch Control
module Branch_Control (
  input  [31:0] Rs,
  input  [25:0] j_destination,
  input  [31:0] Rt,
  input  [31:0] PC,
  input  [15:0] Offset,
  input  Enable,
  input  beq,
  input  bne,
  input  blez,
  input  bgtz,
  input  bltz,
  input  j,
  input  jr,
  output [31:0] new_program_counter
);

  wire and_1_out, and_2_out, and_3_out, and_4_out, and_5_out, equals, next_instruction, or_1_out, or_2_out,
       or_4_out, RS___0, RS___0_t, RS___0_t_t, selector;
  wire [1:0] off;
  wire [31:0] adder_1_out, adder_2_out, multiplexer_1_out, multiplexer_2_out, multiplexer_3_out,
       multiplier_1_cout, undriven;

  and and_1 (and_1_out, beq, equals);
  and and_2 (and_2_out, ~equals, bne);  // AND_Gate
  or or_1 (or_1_out, RS___0, RS___0_t);
  and and_3 (and_3_out, bgtz, RS___0_t_t);
  and and_4 (and_4_out, bltz, RS___0);
  or or_2 (or_2_out, j, jr);
  and and_5 (and_5_out, blez, or_1_out);
  Comparator #(.width(32)) comparator_1 (.a(Rs), .b(Rt), .eq(equals));  // open: gt, lt
  Comparator #(.width(32)) comparator_2 (.a(Rs), .b({32{1'b0}}), .gt(RS___0_t_t), .eq(RS___0_t), .lt(RS___0));
  Comparator #(.width(1)) comparator_3 (.a(jr), .b(1'b1), .eq(selector));  // open: gt, lt
  or or_3 (next_instruction, and_1_out, and_2_out, and_5_out, and_3_out, and_4_out, or_2_out);
  Adder #(.width(32)) adder_1 (.a(PC), .b(32'h4), .out(adder_1_out));  // open: cin, cout
  Adder #(.width(32)) adder_2 (
    .a(adder_1_out), .b({{15{Offset[15]}}, Offset[14:0], off}), .out(adder_2_out));  // open: cin, cout
  Multiplexer #(.width(32), .enable("false")) multiplexer_1 (
    .in0(adder_2_out), .in1(multiplexer_2_out), .out(multiplexer_1_out), .sel(or_4_out));
  Multiplexer #(.width(32), .enable("false")) multiplexer_2 (
    .in0({PC[31:28], j_destination, 2'b00}), .in1(Rs), .out(multiplexer_2_out), .sel(selector));
  Multiplexer #(.width(32), .enable("false")) multiplexer_3 (
    .in0(adder_1_out), .in1(multiplexer_1_out), .out(multiplexer_3_out), .sel(next_instruction));
  or or_4 (or_4_out, j, jr);
  Multiplexer #(.width(32), .enable("false")) multiplexer_4 (
    .in0(PC), .in1(multiplexer_3_out), .out(new_program_counter), .sel(Enable));
  Multiplier #(.width(32)) multiplier_1 (
    .a(undriven), .b(32'h4), .out({{15{Offset[15]}}, Offset[14:0], off}), .cout(multiplier_1_cout));  // open: cin
  // also tied to GND on the sheet: {off[0], off[1]}

  // Other names for the same wires on the sheet: En = Enable; j_PC[31:2] = {PC[31:28], j_destination};
  //   Program_Counter[31:0] = PC; off[31:2] = {{15{Offset[15]}}, Offset[14:0]}

  // Notes on the sheet:
  //   NEXT INSTRUCTION ADDRESS
endmodule
