// Logisim project Instruction Decoder.circ as structural Verilog: 2 circuits, main circuit Instruction Decoder
module Instruction_Decoder (
  input  [31:0] Instruction,
  output nop,
  output mulu,
  output sltu,
  output \xor ,
  output pop,
  output jr,
  output halt,
  output addi,
  output ori,
  output beq,
  output bltz,
  output jump,
  output add,
  output div,
  output \and ,
  output push,
  output mfhi,
  output tty,
  output slti,
  output xori,
  output bne,
  output sub,
  output divu,
  output \or ,
  output mflo,
  output rnd,
  output sltiu,
  output lw,
  output blez,
  output mult,
  output slt,
  output \nor ,
  output kbd,
  output andi,
  output sw,
  output bqtz,
  output [5:0] Op_Code,
  output [4:0] Rs,
  output [4:0] Rt,
  output [4:0] Rd,
  output [4:0] X,
  output [5:0] Func_Code,
  output [15:0] Constante,
  output [25:0] Jump_Dest
);

  wire basic_R_type, equals_1_equals, equals_2_equals, equals_3_equals, equals_4_equals, equals_5_equals,
       equals_6_equals, equals_7_equals, equals_8_equals, equals_9_equals, equals_10_equals,
       equals_11_equals, equals_12_equals, equals_16_equals, equals_17_equals, equals_18_equals,
       equals_19_equals, equals_20_equals, equals_22_equals, equals_23_equals, equals_24_equals,
       equals_25_equals, equals_26_equals, special_R_type, stack_R_type;

  Equals equals_1 (.Const(Instruction[5:0]), .In({6{1'b0}}), .Equals(equals_1_equals));
  Equals equals_2 (.Const(Instruction[5:0]), .In(6'b011001), .Equals(equals_2_equals));
  Equals equals_3 (.Const(Instruction[5:0]), .In(6'b101011), .Equals(equals_3_equals));
  Equals equals_4 (.Const(Instruction[5:0]), .In(6'b101000), .Equals(equals_4_equals));
  Equals equals_5 (.Const(Instruction[5:0]), .In({6{1'b0}}), .Equals(equals_5_equals));
  Equals equals_6 (.Const(Instruction[5:0]), .In({6{1'b1}}), .Equals(equals_6_equals));
  and and_1 (nop, basic_R_type, equals_1_equals);
  and and_2 (mulu, basic_R_type, equals_2_equals);
  and and_3 (sltu, basic_R_type, equals_3_equals);
  and and_4 (\xor , basic_R_type, equals_4_equals);
  and and_5 (pop, stack_R_type, equals_5_equals);
  and and_6 (halt, special_R_type, equals_6_equals);
  Equals equals_7 (.Const(Instruction[5:0]), .In(6'b100000), .Equals(equals_7_equals));
  Equals equals_8 (.Const(Instruction[5:0]), .In(6'b011010), .Equals(equals_8_equals));
  Equals equals_9 (.Const(Instruction[5:0]), .In(6'b100100), .Equals(equals_9_equals));
  Equals equals_10 (.Const(Instruction[5:0]), .In(6'b001000), .Equals(equals_10_equals));
  Equals equals_11 (.Const(Instruction[5:0]), .In(6'b000001), .Equals(equals_11_equals));
  Equals equals_12 (.Const(Instruction[5:0]), .In(6'b000001), .Equals(equals_12_equals));
  and and_7 (add, basic_R_type, equals_7_equals);
  and and_8 (div, basic_R_type, equals_8_equals);
  and and_9 (\and , basic_R_type, equals_9_equals);
  and and_10 (jr, basic_R_type, equals_10_equals);
  and and_11 (push, stack_R_type, equals_11_equals);
  and and_12 (tty, special_R_type, equals_12_equals);
  Equals equals_13 (.Const(Instruction[31:26]), .In({6{1'b0}}), .Equals(basic_R_type));
  Equals equals_14 (.Const(Instruction[31:26]), .In(6'b111000), .Equals(stack_R_type));
  Equals equals_15 (.Const(Instruction[31:26]), .In({6{1'b1}}), .Equals(special_R_type));
  and and_13 (sub, basic_R_type, equals_16_equals);
  Equals equals_16 (.Const(Instruction[5:0]), .In(6'b100010), .Equals(equals_16_equals));
  and and_14 (divu, basic_R_type, equals_17_equals);
  Equals equals_17 (.Const(Instruction[5:0]), .In(6'b011011), .Equals(equals_17_equals));
  and and_15 (\or , basic_R_type, equals_18_equals);
  Equals equals_18 (.Const(Instruction[5:0]), .In(6'b100101), .Equals(equals_18_equals));
  and and_16 (mfhi, basic_R_type, equals_19_equals);
  Equals equals_19 (.Const(Instruction[5:0]), .In(6'b010000), .Equals(equals_19_equals));
  and and_17 (rnd, special_R_type, equals_20_equals);
  Equals equals_20 (.Const(Instruction[5:0]), .In(6'b000010), .Equals(equals_20_equals));
  Equals equals_21 (.Const(Instruction[31:26]), .In(6'b000010), .Equals(jump));
  and and_18 (mult, basic_R_type, equals_22_equals);
  Equals equals_22 (.Const(Instruction[5:0]), .In(6'b011000), .Equals(equals_22_equals));
  and and_19 (slt, basic_R_type, equals_23_equals);
  Equals equals_23 (.Const(Instruction[5:0]), .In(6'b101010), .Equals(equals_23_equals));
  and and_20 (\nor , basic_R_type, equals_24_equals);
  Equals equals_24 (.Const(Instruction[5:0]), .In(6'b100111), .Equals(equals_24_equals));
  and and_21 (mflo, basic_R_type, equals_25_equals);
  Equals equals_25 (.Const(Instruction[5:0]), .In(6'b010010), .Equals(equals_25_equals));
  and and_22 (kbd, special_R_type, equals_26_equals);
  Equals equals_26 (.Const(Instruction[5:0]), .In(6'b000100), .Equals(equals_26_equals));
  Equals equals_27 (.Const(Instruction[31:26]), .In(6'b001000), .Equals(addi));
  Equals equals_28 (.Const(Instruction[31:26]), .In(6'b001101), .Equals(ori));
  Equals equals_29 (.Const(Instruction[31:26]), .In(6'b000100), .Equals(beq));
  Equals equals_30 (.Const(Instruction[31:26]), .In(6'b000001), .Equals(bltz));
  Equals equals_31 (.Const(Instruction[31:26]), .In(6'b001010), .Equals(slti));
  Equals equals_32 (.Const(Instruction[31:26]), .In(6'b001110), .Equals(xori));
  Equals equals_33 (.Const(Instruction[31:26]), .In(6'b000101), .Equals(bne));
  Equals equals_34 (.Const(Instruction[31:26]), .In(6'b001011), .Equals(sltiu));
  Equals equals_35 (.Const(Instruction[31:26]), .In(6'b100011), .Equals(lw));
  Equals equals_36 (.Const(Instruction[31:26]), .In(6'b000110), .Equals(blez));
  Equals equals_37 (.Const(Instruction[31:26]), .In(6'b001100), .Equals(andi));
  Equals equals_38 (.Const(Instruction[31:26]), .In(6'b101011), .Equals(sw));
  Equals equals_39 (.Const(Instruction[31:26]), .In(6'b000111), .Equals(bqtz));

  assign Constante = Instruction[31:16];
  assign Func_Code = Instruction[5:0];
  assign Jump_Dest = Instruction[31:6];
  assign Op_Code = Instruction[31:26];
  assign Rd = Instruction[15:11];
  assign Rs = Instruction[25:21];
  assign Rt = Instruction[20:16];
  assign X = Instruction[10:6];

  // Other names for the same wires on the sheet: Const[15:0] = Instruction[31:16]

  // Notes on the sheet:
  //   Basic R-Types
  //   Stack R-Types
  //   Special R-Types
  //   Spliter
  //   R-Types
  //   J Type
  //   I-Types
  //   Outputs
endmodule

module Equals (
  input  [5:0] Const,
  input  [5:0] In,
  output Equals
);

  Comparator #(.width(6)) comparator_1 (.a(Const), .b(In), .eq(Equals));  // open: gt, lt
endmodule
