// Logisim project Program Counter.circ as structural Verilog: 1 circuit, main circuit Program Counter
module Program_Counter (
  input  [31:0] Inst_In,
  input  Enable,
  input  Clock,
  input  Reset,
  output [31:0] Inst_Out
);

  Register #(.width(32)) register_1 (.D(Inst_In), .en(Enable), .Q(Inst_Out), .clk(Clock), .clr(Reset));
endmodule
