// Logisim project RAM Handler.circ as structural Verilog: 4 circuits, main circuit RAM Reader
module RAM_Reader (
  input  [31:0] RAM_O1,
  input  [31:0] RAM_O2,
  input  [31:0] RAM_O3,
  input  [31:0] RAM_O4,
  input  [31:0] Instruction_Address,
  input  Enable,
  input  Clock,
  input  Clear,
  input  [3:0] Read_time,
  output [15:0] Address,
  output [31:0] Ram_Data,
  output Dead_time,
  output Chip_Select
);

  wire Chip_Select_t, temporizer_1_dead_time;
  wire [31:0] little_i_invert_1_out_2, multiplexer_1_out;

  Temporizer temporizer_1 (
    .Time(Read_time), .Clock(Clock), .Enable(Enable), .Dead_Time(temporizer_1_dead_time),
    .Chip_Select(Chip_Select));
  Multiplexer #(.select(2), .width(32), .enable("false")) multiplexer_1 (
    .in0(RAM_O1), .in1(RAM_O2), .in2(RAM_O3), .in3(RAM_O4), .out(multiplexer_1_out),
    .sel(Instruction_Address[3:2]));
  Little_I_Invert little_i_invert_1 (.In(multiplexer_1_out), .out_2(little_i_invert_1_out_2));
  Register #(.width(32)) register_1 (
    .D(little_i_invert_1_out_2), .en(Chip_Select_t), .Q(Ram_Data), .clk(Clock), .clr(Clear));
  D_Flip_Flop d_ff_1 (.clk(Clock), .D(temporizer_1_dead_time), .Q(Dead_time));  // open: Qn, preset, en, reset

  assign Address = Instruction_Address[19:4];

  // Other names for the same wires on the sheet: addrs[15:0] = Instruction_Address[19:4]

  // Notes on the sheet:
  //   Bank Selector
  //   16bits address
endmodule

module Little_I_Invert (
  input  [31:0] In,
  output [31:0] out_2
);


  assign out_2 = {In[7:0], In[15:8], In[23:16], In[31:24]};
endmodule

module Temporizer (
  input  [3:0] Time,
  input  Clock,
  input  Enable,
  output Dead_Time,
  output Chip_Select
);

  wire _0, and_1_out, d_ff_1_q, demultiplexer_1_out0, running;
  wire [3:0] counter_1_q;

  or or_1 (running, Enable, and_1_out);
  and and_1 (and_1_out, demultiplexer_1_out0, ~_0);  // AND_Gate
  Counter #(.width(4), .max('hf)) counter_1 (
    .load(running), .D(Time), .count(and_1_out), .Q(counter_1_q), .clk(Clock));  // open: carry, clr
  D_Flip_Flop d_ff_1 (.clk(Clock), .D(running), .Q(d_ff_1_q));  // open: Qn, preset, en, reset
  Comparator #(.width(4)) comparator_1 (.a(counter_1_q), .b(4'b0000), .eq(_0));  // open: gt, lt
  Demultiplexer #(.enable("false")) demultiplexer_1 (
    .out0(demultiplexer_1_out0), .out1(Dead_Time), .in(d_ff_1_q), .sel(_0));
  or or_2 (Chip_Select, Dead_Time, running);
endmodule

module RAM_Writer (
  input  [31:0] Data,
  input  Enable,
  input  Clock,
  input  Clear,
  input  [3:0] Read_time,
  input  [31:0] Instruction_Address,
  output [31:0] RAM_I1,
  output [31:0] RAM_I2,
  output [31:0] RAM_I3,
  output [3:0] Bank_Mask,
  output [31:0] RAM_I4,
  output [15:0] Address,
  output Dead_time,
  output Chip_Select
);

  wire [31:0] little_i_invert_1_out_2, register_1_q;

  Little_I_Invert little_i_invert_1 (.In(Data), .out_2(little_i_invert_1_out_2));
  Decoder #(.select(2), .enable("false")) decoder_1 (
    .out0(Bank_Mask[0]), .out1(Bank_Mask[1]), .out2(Bank_Mask[2]), .out3(Bank_Mask[3]),
    .sel(Instruction_Address[3:2]));
  Temporizer temporizer_1 (
    .Time(Read_time), .Clock(Clock), .Enable(Enable), .Dead_Time(Dead_time), .Chip_Select(Chip_Select));
  Register #(.width(32)) register_1 (
    .D(little_i_invert_1_out_2), .en(Chip_Select), .Q(register_1_q), .clk(Clock), .clr(Clear));
  Demultiplexer #(.select(2), .width(32), .enable("false")) demultiplexer_1 (
    .out0(RAM_I1), .out1(RAM_I2), .out2(RAM_I3), .out3(RAM_I4), .in(register_1_q),
    .sel(Instruction_Address[3:2]));

  assign Address = Instruction_Address[19:4];

  // Other names for the same wires on the sheet: En = Enable; RT[3:0] = Read_time

  // Notes on the sheet:
  //   Bank Selector
  //   16bits address
endmodule
