// Logisim project Register File.circ as structural Verilog: 1 circuit, main circuit Register File
module Register_File (
  input  [31:0] Input,
  input  [4:0] In_Selector,
  input  [4:0] Out1_Selector,
  input  Clock,
  input  [1:0] Hi_Lo_Instruction,
  input  [4:0] Out2_Selector,
  input  Reset,
  input  [1:0] Stack_Instruction,
  input  Read_Write,
  output [31:0] Get1,
  output [31:0] Get2,
  output [31:0] Get_Hi_Lo
);

  wire and_1_out, and_2_out, En0, En1, En2, En3, En4, En5, En6, En7, En8, En9, En10, En11, En12, En13, En14,
       En15, En16, En17, En18, En19, En20, En21, En22, En23, En24, En25, En26, En27, En28, En29, En30, En31;
  wire [31:0] adder_1_out, Hi_q, Lo_q, multiplexer_1_out, multiplexer_2_out, o0, o1, o2, o3, o4, o5, o6, o7,
       o8, o9, o10, o11, o12, o13, o14, o15, o16, o17, o18, o19, o20, o21, o22, o23, o24, o25, o26, o27, o28,
       o29, o30, sp;

  Register #(.width(32)) R0 (.D(Input), .en(En0), .Q(o0), .clk(Clock), .clr(Reset));
  Register #(.width(32)) R4 (.D(Input), .en(En4), .Q(o4), .clk(Clock), .clr(Reset));
  Register #(.width(32)) R8 (.D(Input), .en(En8), .Q(o8), .clk(Clock), .clr(Reset));
  Register #(.width(32)) R12 (.D(Input), .en(En12), .Q(o12), .clk(Clock), .clr(Reset));
  Register #(.width(32)) R16 (.D(Input), .en(En16), .Q(o16), .clk(Clock), .clr(Reset));
  Register #(.width(32)) R20 (.D(Input), .en(En20), .Q(o20), .clk(Clock), .clr(Reset));
  Register #(.width(32)) R24 (.D(Input), .en(En24), .Q(o24), .clk(Clock), .clr(Reset));
  Register #(.width(32)) R28 (.D(Input), .en(En28), .Q(o28), .clk(Clock), .clr(Reset));
  Register #(.width(32)) R1 (.D(Input), .en(En1), .Q(o1), .clk(Clock), .clr(Reset));
  Register #(.width(32)) R5 (.D(Input), .en(En5), .Q(o5), .clk(Clock), .clr(Reset));
  Register #(.width(32)) R9 (.D(Input), .en(En9), .Q(o9), .clk(Clock), .clr(Reset));
  Register #(.width(32)) R13 (.D(Input), .en(En13), .Q(o13), .clk(Clock), .clr(Reset));
  Register #(.width(32)) R17 (.D(Input), .en(En17), .Q(o17), .clk(Clock), .clr(Reset));
  Register #(.width(32)) R21 (.D(Input), .en(En21), .Q(o21), .clk(Clock), .clr(Reset));
  Register #(.width(32)) R25 (.D(Input), .en(En25), .Q(o25), .clk(Clock), .clr(Reset));
  Register #(.width(32)) R29 (.D(Input), .en(En29), .Q(o29), .clk(Clock), .clr(Reset));
  Register #(.width(32)) R2 (.D(Input), .en(En2), .Q(o2), .clk(Clock), .clr(Reset));
  Register #(.width(32)) R6 (.D(Input), .en(En6), .Q(o6), .clk(Clock), .clr(Reset));
  Register #(.width(32)) R10 (.D(Input), .en(En10), .Q(o10), .clk(Clock), .clr(Reset));
  Register #(.width(32)) R14 (.D(Input), .en(En14), .Q(o14), .clk(Clock), .clr(Reset));
  Register #(.width(32)) R18 (.D(Input), .en(En18), .Q(o18), .clk(Clock), .clr(Reset));
  Register #(.width(32)) R22 (.D(Input), .en(En22), .Q(o22), .clk(Clock), .clr(Reset));
  Register #(.width(32)) R26 (.D(Input), .en(En26), .Q(o26), .clk(Clock), .clr(Reset));
  Register #(.width(32)) R30 (.D(Input), .en(En30), .Q(o30), .clk(Clock), .clr(Reset));
  Multiplexer #(.width(32), .enable("false")) multiplexer_1 (
    .in0(32'hfffffffc), .in1(32'h4), .out(multiplexer_1_out), .sel(Stack_Instruction[0]));
  Register #(.width(32)) R3 (.D(Input), .en(En3), .Q(o3), .clk(Clock), .clr(Reset));
  Register #(.width(32)) R7 (.D(Input), .en(En7), .Q(o7), .clk(Clock), .clr(Reset));
  Register #(.width(32)) R11 (.D(Input), .en(En11), .Q(o11), .clk(Clock), .clr(Reset));
  Register #(.width(32)) R15 (.D(Input), .en(En15), .Q(o15), .clk(Clock), .clr(Reset));
  Register #(.width(32)) R19 (.D(Input), .en(En19), .Q(o19), .clk(Clock), .clr(Reset));
  Register #(.width(32)) R23 (.D(Input), .en(En23), .Q(o23), .clk(Clock), .clr(Reset));
  Register #(.width(32)) R27 (.D(Input), .en(En27), .Q(o27), .clk(Clock), .clr(Reset));
  Adder #(.width(32)) adder_1 (.a(multiplexer_1_out), .b(sp), .out(adder_1_out));  // open: cin, cout
  Multiplexer #(.width(32), .enable("false")) multiplexer_2 (
    .in0(Input), .in1(adder_1_out), .out(multiplexer_2_out), .sel(Stack_Instruction[1]));
  Demultiplexer #(.select(5), .enable("false")) demultiplexer_1 (
    .out0(En0), .out1(En1), .out2(En2), .out3(En3), .out4(En4), .out5(En5), .out6(En6), .out7(En7),
    .out8(En8), .out9(En9), .out10(En10), .out11(En11), .out12(En12), .out13(En13), .out14(En14),
    .out15(En15), .out16(En16), .out17(En17), .out18(En18), .out19(En19), .out20(En20), .out21(En21),
    .out22(En22), .out23(En23), .out24(En24), .out25(En25), .out26(En26), .out27(En27), .out28(En28),
    .out29(En29), .out30(En30), .out31(En31), .in(Read_Write), .sel(In_Selector));
  Register #(.width(32)) R31 (.D(multiplexer_2_out), .en(En31), .Q(sp), .clk(Clock), .clr(Reset));
  and and_1 (and_1_out, Hi_Lo_Instruction[0], Hi_Lo_Instruction[1]);
  and and_2 (and_2_out, Hi_Lo_Instruction[0], ~Hi_Lo_Instruction[1]);  // AND_Gate
  Multiplexer #(.select(5), .width(32), .enable("false")) multiplexer_3 (
    .in0(o0), .in1(o1), .in2(o2), .in3(o3), .in4(o4), .in5(o5), .in6(o6), .in7(o7), .in8(o8), .in9(o9),
    .in10(o10), .in11(o11), .in12(o12), .in13(o13), .in14(o14), .in15(o15), .in16(o16), .in17(o17),
    .in18(o18), .in19(o19), .in20(o20), .in21(o21), .in22(o22), .in23(o23), .in24(o24), .in25(o25),
    .in26(o26), .in27(o27), .in28(o28), .in29(o29), .in30(o30), .in31(sp), .out(Get1), .sel(Out1_Selector));
  Register #(.width(32)) Hi (.D(Input), .en(and_1_out), .Q(Hi_q), .clk(Clock), .clr(Reset));
  Register #(.width(32)) Lo (.D(Input), .en(and_2_out), .Q(Lo_q), .clk(Clock), .clr(Reset));
  Multiplexer #(.width(32), .enable("false")) multiplexer_4 (
    .in0(Lo_q), .in1(Hi_q), .out(Get_Hi_Lo), .sel(Hi_Lo_Instruction[1]));
  Multiplexer #(.select(5), .width(32), .enable("false")) multiplexer_5 (
    .in0(o0), .in1(o1), .in2(o2), .in3(o3), .in4(o4), .in5(o5), .in6(o6), .in7(o7), .in8(o8), .in9(o9),
    .in10(o10), .in11(o11), .in12(o12), .in13(o13), .in14(o14), .in15(o15), .in16(o16), .in17(o17),
    .in18(o18), .in19(o19), .in20(o20), .in21(o21), .in22(o22), .in23(o23), .in24(o24), .in25(o25),
    .in26(o26), .in27(o27), .in28(o28), .in29(o29), .in30(o30), .in31(sp), .out(Get2), .sel(Out2_Selector));

  // Other names for the same wires on the sheet: Clk = Clock; H_L_select[1:0] = Hi_Lo_Instruction; in[31:0] = Input;
  //   r_w = Read_Write; Stack_select[1:0] = Stack_Instruction

  // Notes on the sheet:
  //   Registers
  //   Register Enable
  //   Register Out1
  //   Register Out2
endmodule
