// Logisim project s-mips.circ as structural Verilog: 4 circuits, main circuit S-MIPS Board
module S_MIPS_Board (
  input  DESHABILITAR_DISPATCHER,
  output halt
);

  wire button_1_out, CLK, CS, d_ff_1_q, LCLR, LoadRAM, LoadRAMOn, LW, R_R_W, R_W, ram_dispatcher_1_finished,
       RCS, Reset_out, RST, TTY_EN;
  wire [2:0] KDB;
  wire [3:0] LMask, Mask, ram_1_read_time, ram_1_write_time, RMask;
  wire [6:0] KDB_DATA, TTY_DATA;
  wire [15:0] Addr, LAddr, RAddr;
  wire [31:0] I0, I1, I2, I3, LData, ram_1_data_out_0, ram_1_data_out_1, ram_1_data_out_2, ram_1_data_out_3,
       RI0, RI1, RI2, RI3;

  TTY #(.rows(25), .cols(80)) tty_1 (.data(TTY_DATA), .clk(CLK), .we(TTY_EN), .clr(RST));
  not not_1 (LoadRAMOn, ram_dispatcher_1_finished);
  RAM_Dispatcher ram_dispatcher_1 (
    .WriteTime(ram_1_write_time), .Clock(CLK), .Data(LData), .Address(LAddr), .Mask(LMask),
    .Finished(ram_dispatcher_1_finished), .Write(LW), .CLR(LCLR));
  Keyboard #(.buflen(64)) keyboard_1 (.clk(CLK), .re(KDB[0]), .avail(KDB[2]), .data(KDB_DATA));  // open: clr
  RAM ram_1 (
    .Address(RAddr), .Data_Out_0(ram_1_data_out_0), .Data_Out_1(ram_1_data_out_1),
    .Data_Out_2(ram_1_data_out_2), .Data_Out_3(ram_1_data_out_3), .Data_In_0(RI0), .Data_In_1(RI1),
    .Data_In_2(RI2), .Data_In_3(RI3), .Mask(RMask), .nRead_Write(R_R_W), .Chip_Select(RCS),
    .Read_Time(ram_1_read_time), .Reset(button_1_out), .Write_Time(ram_1_write_time));
  Button button_1 (.out(button_1_out));
  D_Flip_Flop d_ff_1 (.clk(CLK), .D(1'b1), .Q(d_ff_1_q), .reset(Reset_out));  // open: Qn, preset, en
  Button Reset (.out(Reset_out));
  S_MIPS s_mips_1 (
    .Kbd_Enable(KDB[0]), .Address(Addr), .Kbd_Clear(KDB[1]), .Kbd_Available(KDB[2]), .RAM_In_0(I0),
    .Kbd_ASCII_Data(KDB_DATA), .RAM_In_1(I1), .TTY_Enable(TTY_EN), .RAM_In_2(I2), .RAM_In_3(I3),
    .TTY_ASCII_Data(TTY_DATA), .Reset(RST), .RAM_Out_0(ram_1_data_out_0), .Clock(CLK),
    .RAM_Out_1(ram_1_data_out_1), .Stop(halt), .RAM_Out_2(ram_1_data_out_2), .RAM_Out_3(ram_1_data_out_3),
    .Mask(Mask), .Read_Time(ram_1_read_time), .Write_Time(ram_1_write_time), .nRead_Write(R_W),
    .Chip_Select(CS));
  D_Flip_Flop d_ff_2 (.clk(CLK), .D(d_ff_1_q), .Qn(LCLR), .reset(Reset_out));  // open: Q, preset, en
  or or_1 (RST, LCLR, LoadRAM);
  Clock clock_1 (.out(CLK));
  Multiplexer #(.width(32), .enable("false")) multiplexer_1 (.in0(I0), .in1(LData), .out(RI0), .sel(LoadRAM));
  Multiplexer #(.width(32), .enable("false")) multiplexer_2 (.in0(I1), .in1(LData), .out(RI1), .sel(LoadRAM));
  Multiplexer #(.width(32), .enable("false")) multiplexer_3 (.in0(I2), .in1(LData), .out(RI2), .sel(LoadRAM));
  Multiplexer #(.width(32), .enable("false")) multiplexer_4 (.in0(I3), .in1(LData), .out(RI3), .sel(LoadRAM));
  and and_1 (LoadRAM, ~DESHABILITAR_DISPATCHER, LoadRAMOn);  // AND_Gate
  Multiplexer #(.width(16), .enable("false")) multiplexer_5 (.in0(Addr), .in1(LAddr), .out(RAddr), .sel(LoadRAM));
  Multiplexer #(.width(4), .enable("false")) multiplexer_6 (.in0(Mask), .in1(LMask), .out(RMask), .sel(LoadRAM));
  Multiplexer #(.enable("false")) multiplexer_7 (.in0(CS), .in1(LW), .out(RCS), .sel(LoadRAM));
  Multiplexer #(.enable("false")) multiplexer_8 (.in0(R_W), .in1(LW), .out(R_R_W), .sel(LoadRAM));

  // Notes on the sheet:
  //   NO MODIFICAR
  //   Keyboard
endmodule

module RAM (
  input  [15:0] Address,
  input  [31:0] Data_In_0,
  input  [31:0] Data_In_1,
  input  [31:0] Data_In_2,
  input  [31:0] Data_In_3,
  input  [3:0] Mask,
  input  nRead_Write,
  input  Chip_Select,
  input  Reset,
  output [31:0] Data_Out_0,
  output [31:0] Data_Out_1,
  output [31:0] Data_Out_2,
  output [31:0] Data_Out_3,
  output [3:0] Read_Time,
  output [3:0] Write_Time
);

  wire and_2_out, and_3_out, and_4_out, and_5_out, and_6_out, and_7_out, and_8_out, and_9_out, Changed, CLK,
       comparator_2_eq, comparator_3_eq, comparator_4_eq, comparator_5_eq, comparator_6_eq, Count,
       demultiplexer_3_out0, Idle, Idle_q, Load, Load0, Load1, nand_1_out, or_1_out, or_2_out, or_3_out,
       or_4_out, or_5_out, or_6_out, or_7_out, or_8_out, or_9_out, or_10_out, Proc_q, Update_Mem, Zero_Time;
  wire [3:0] counter_1_q, multiplexer_1_out, subtractor_1_out;
  wire [31:0] register_1_q, register_2_q, register_3_q, register_4_q, register_5_q;

  // Probe on 4'b0011
  // Probe on 4'b0010
  Multiplexer #(.width(4), .enable("false")) multiplexer_1 (
    .in0(4'b0011), .in1(4'b0010), .out(multiplexer_1_out), .sel(nRead_Write));
  or or_1 (or_1_out, Idle, Update_Mem);
  or or_2 (or_2_out, ~Chip_Select, Reset);  // OR_Gate
  Subtractor #(.width(4)) subtractor_1 (.a(multiplexer_1_out), .b(4'b0010), .out(subtractor_1_out));  // open: bin, bout
  Demultiplexer #(.enable("false")) demultiplexer_1 (.out0(Idle), .out1(Load0), .in(Idle_q), .sel(Changed));
  D_Flip_Flop u_Idle (.clk(CLK), .D(or_1_out), .Q(Idle_q), .preset(or_2_out));  // open: Qn, en, reset
  // Probe on counter_1_q
  Counter #(.width(4), .max('hf)) counter_1 (
    .load(Load), .D(subtractor_1_out), .count(Count), .Q(counter_1_q), .clk(CLK), .clr(or_3_out));  // open: carry
  or or_3 (or_3_out, ~Chip_Select, Reset);  // OR_Gate
  Comparator #(.width(4), .mode("unsigned")) comparator_1 (
    .a(4'b0000), .b(counter_1_q), .eq(Zero_Time));  // open: gt, lt
  or or_4 (or_4_out, Count, Load0, Load1);
  Register #(.width(32)) register_1 (.D(Data_In_0), .en(Chip_Select), .Q(register_1_q), .clk(CLK), .clr(or_5_out));
  or or_5 (or_5_out, ~Chip_Select, Reset);  // OR_Gate
  Register #(.width(32)) register_2 (.D(Data_In_1), .en(Chip_Select), .Q(register_2_q), .clk(CLK), .clr(or_6_out));
  or or_6 (or_6_out, ~Chip_Select, Reset);  // OR_Gate
  Register #(.width(32)) register_3 (.D(Data_In_2), .en(Chip_Select), .Q(register_3_q), .clk(CLK), .clr(or_7_out));
  or or_7 (or_7_out, ~Chip_Select, Reset);  // OR_Gate
  Register #(.width(32)) register_4 (.D(Data_In_3), .en(Chip_Select), .Q(register_4_q), .clk(CLK), .clr(or_8_out));
  or or_8 (or_8_out, ~Chip_Select, Reset);  // OR_Gate
  Register #(.width(32)) register_5 (
    .D({{11{1'b1}}, nRead_Write, Mask, Address}), .en(Chip_Select), .Q(register_5_q), .clk(CLK),
    .clr(or_9_out));
  or or_9 (or_9_out, ~Chip_Select, Reset);  // OR_Gate
  D_Flip_Flop Proc (.clk(CLK), .D(or_4_out), .Q(Proc_q), .reset(or_10_out));  // open: Qn, preset, en
  or or_10 (or_10_out, ~Chip_Select, Reset);  // OR_Gate
  Demultiplexer #(.enable("false")) demultiplexer_2 (
    .out0(Count), .out1(Update_Mem), .in(demultiplexer_3_out0), .sel(Zero_Time));
  Demultiplexer #(.enable("false")) demultiplexer_3 (
    .out0(demultiplexer_3_out0), .out1(Load1), .in(Proc_q), .sel(Changed));
  Clock clock_1 (.out(CLK));
  Comparator #(.width(32)) comparator_2 (.a(register_1_q), .b(Data_In_0), .eq(comparator_2_eq));  // open: gt, lt
  Comparator #(.width(32)) comparator_3 (.a(register_2_q), .b(Data_In_1), .eq(comparator_3_eq));  // open: gt, lt
  Comparator #(.width(32)) comparator_4 (.a(register_3_q), .b(Data_In_2), .eq(comparator_4_eq));  // open: gt, lt
  Comparator #(.width(32)) comparator_5 (.a(register_4_q), .b(Data_In_3), .eq(comparator_5_eq));  // open: gt, lt
  Comparator #(.width(32)) comparator_6 (
    .a(register_5_q), .b({{11{1'b1}}, nRead_Write, Mask, Address}), .eq(comparator_6_eq));  // open: gt, lt
  nand nand_1 (nand_1_out, comparator_6_eq, comparator_2_eq, comparator_3_eq, comparator_4_eq, comparator_5_eq);
  and and_1 (Changed, nand_1_out, Chip_Select);
  or or_11 (Load, Count, Load1, Load0);
  and and_2 (and_2_out, Mask[0], Update_Mem, nRead_Write);
  and and_3 (and_3_out, Mask[1], Update_Mem, nRead_Write);
  and and_4 (and_4_out, Mask[2], Update_Mem, nRead_Write);
  and and_5 (and_5_out, Mask[3], Update_Mem, nRead_Write);
  RAM_part #(.addrWidth(16), .dataWidth(32), .bus("separate")) ram_1 (
    .addr(Address), .din(Data_In_0), .data(Data_Out_0), .str(and_2_out), .sel(Chip_Select), .clk(CLK),
    .ld(and_6_out), .clr(Reset));
  and and_6 (and_6_out, ~nRead_Write, Idle);  // AND_Gate
  RAM_part #(.addrWidth(16), .dataWidth(32), .bus("separate")) ram_2 (
    .addr(Address), .din(Data_In_1), .data(Data_Out_1), .str(and_3_out), .sel(Chip_Select), .clk(CLK),
    .ld(and_7_out), .clr(Reset));
  and and_7 (and_7_out, ~nRead_Write, Idle);  // AND_Gate
  RAM_part #(.addrWidth(16), .dataWidth(32), .bus("separate")) ram_3 (
    .addr(Address), .din(Data_In_2), .data(Data_Out_2), .str(and_4_out), .sel(Chip_Select), .clk(CLK),
    .ld(and_8_out), .clr(Reset));
  and and_8 (and_8_out, ~nRead_Write, Idle);  // AND_Gate
  RAM_part #(.addrWidth(16), .dataWidth(32), .bus("separate")) ram_4 (
    .addr(Address), .din(Data_In_3), .data(Data_Out_3), .str(and_5_out), .sel(Chip_Select), .clk(CLK),
    .ld(and_9_out), .clr(Reset));
  and and_9 (and_9_out, ~nRead_Write, Idle);  // AND_Gate

  assign Read_Time = 4'b0011;
  assign Write_Time = 4'b0010;

  // Other names for the same wires on the sheet: M0 = Mask[0]; M1 = Mask[1]; M2 = Mask[2]; M3 = Mask[3];
  //   RW = nRead_Write; CLR = Reset; CS = Chip_Select; Load2 = Count

  // Notes on the sheet:
  //   NO MODIFICAR
  //   excepto quizás los valores RT y WT
  //   BANK0
  //   BANK1
  //   BANK2
  //   BANK3
endmodule

module S_MIPS (
  input  Kbd_Available,
  input  [6:0] Kbd_ASCII_Data,
  input  [31:0] RAM_Out_0,
  input  [31:0] RAM_Out_1,
  input  Reset,
  input  [31:0] RAM_Out_2,
  input  Clock,
  input  [31:0] RAM_Out_3,
  input  [3:0] Read_Time,
  input  [3:0] Write_Time,
  output Kbd_Enable,
  output [15:0] Address,
  output Kbd_Clear,
  output TTY_Enable,
  output [6:0] TTY_ASCII_Data,
  output Stop,
  output [31:0] RAM_In_0,
  output [31:0] RAM_In_1,
  output [31:0] RAM_In_2,
  output [31:0] RAM_In_3,
  output [3:0] Mask,
  output nRead_Write,
  output Chip_Select
);

  wire add, addi, alu_1_carry, alu_1_sf, alu_1_zf, ALU_flag, \and , and_3_out, and_4_out, and_7_out, andi,
       beq, bgtz, blez, bltz, bne, CLK, CS_reader, d_ff_1_q, div, divu, DT_Reader, DT_Writer, En_Cu, En_IM,
       En_rnd, halt, HiLo_Type, I_Type, IM_Chip_Select, instr_loaded, jr, jump, kbd, lw, mfhi, mflo, minus_1,
       mult, mulu, Next, nop, \nor , not_1_out, \or , or_2_out, or_3_out, or_4_out, or_5_out, or_6_out,
       or_7_out, or_9_out, ori, patch, pop, pop_enable, push, push_enable, push_pop, RAM_R_Type, read_RAM,
       rnd, Sign, slt, slti, sltiu, sltu, stack_flag, sub, sw, this_op, tty, write_RAM, write_RF, \xor , xori;
  wire [1:0] Rf_in_select;
  wire [3:0] ALU_selector;
  wire [4:0] multiplexer_12_out, Rd, Rs, Rt, X;
  wire [5:0] func_code, op_code;
  wire [15:0] im_addr, immediate, multiplexer_3_out, read_addr, write_addr;
  wire [25:0] jump_dest;
  wire [31:0] ALU_out, bit_extender_1_out, bit_extender_2_out, extended_imm, Hi, in_Pc, kbd_data32, Lo,
       multiplexer_2_out, multiplexer_5_out, multiplexer_6_out, multiplexer_7_out, multiplexer_8_out,
       multiplexer_9_out, multiplexer_10_out, multiplexer_11_out, out_PC, Ram_Data, ram_reader_1_ram_data,
       random_1_out, register_1_q, remainder, Rt_t, Sp;
  wire [31:7] Rs_t;

  or or_1 (Chip_Select, IM_Chip_Select, CS_reader, nRead_Write);
  or or_2 (or_2_out, DT_Writer, Next, DT_Reader);
  assign bit_extender_1_out = {{16{1'b0}}, immediate};  // Bit_Extender bit_extender_1
  assign bit_extender_2_out = {{16{immediate[15]}}, immediate};  // Bit_Extender bit_extender_2
  // Probe on out_PC
  Program_Counter program_counter_1 (.Inst_In(in_Pc), .Enable(or_2_out), .Clock(CLK), .Inst_Out(out_PC), .Reset(Reset));
  Multiplexer #(.width(32), .enable("false")) multiplexer_1 (
    .in0(bit_extender_1_out), .in1(bit_extender_2_out), .out(extended_imm), .sel(or_3_out));
  or or_3 (or_3_out, sw, sltiu, slti, addi, lw);
  and and_1 (CLK, Clock, ~Stop);  // AND_Gate
  assign kbd_data32 = {{25{1'b0}}, Kbd_ASCII_Data};  // Bit_Extender bit_extender_3
  // Probe on extended_imm
  and and_2 (minus_1, Kbd_Enable, ~Kbd_Available);  // AND_Gate
  RAM_Reader ram_reader_1 (
    .Instruction_Address(out_PC), .Enable(En_IM), .Clock(CLK), .Clear(Reset), .Read_time(Read_Time),
    .Address(im_addr), .Ram_Data(ram_reader_1_ram_data), .Dead_time(instr_loaded),
    .Chip_Select(IM_Chip_Select), .RAM_O1(RAM_Out_0), .RAM_O2(RAM_Out_1), .RAM_O3(RAM_Out_2),
    .RAM_O4(RAM_Out_3));
  or or_4 (or_4_out, push_enable, write_RAM);
  Instruction_Decoder instruction_decoder_1 (
    .Instruction(ram_reader_1_ram_data), .nop(nop), .mulu(mulu), .sltu(sltu), .\xor (\xor ), .pop(pop),
    .jr(jr), .halt(halt), .addi(addi), .ori(ori), .beq(beq), .bltz(bltz), .jump(jump), .add(add), .div(div),
    .\and (\and ), .push(push), .mfhi(mfhi), .tty(tty), .slti(slti), .xori(xori), .bne(bne), .sub(sub),
    .divu(divu), .\or (\or ), .mflo(mflo), .rnd(rnd), .sltiu(sltiu), .lw(lw), .blez(blez), .mult(mult),
    .slt(slt), .\nor (\nor ), .kbd(kbd), .andi(andi), .sw(sw), .bqtz(bgtz), .Op_Code(op_code), .Rs(Rs),
    .Rt(Rt), .Rd(Rd), .X(X), .Func_Code(func_code), .Constante(immediate), .Jump_Dest(jump_dest));
  Branch_Control branch_control_1 (
    .Rs({Rs_t, TTY_ASCII_Data}), .j_destination(jump_dest), .Rt(Rt_t), .PC(out_PC), .Offset(immediate),
    .beq(beq), .bne(bne), .blez(blez), .bgtz(bgtz), .bltz(bltz), .j(jump), .jr(jr),
    .new_program_counter(in_Pc), .Enable(or_2_out));
  and and_3 (and_3_out, read_RAM, ~DT_Reader);  // AND_Gate
  and and_4 (and_4_out, or_4_out, ~DT_Writer);  // AND_Gate
  or or_5 (or_5_out, En_Cu, patch);
  or or_6 (or_6_out, and_3_out, and_4_out);
  and and_5 (En_IM, or_5_out, ~or_6_out);  // AND_Gate
  D_Flip_Flop d_ff_1 (.clk(CLK), .D(Reset), .Q(d_ff_1_q));  // open: Qn, preset, en, reset
  and and_6 (patch, d_ff_1_q, ~Reset);  // AND_Gate
  Multiplexer #(.width(32), .enable("false")) multiplexer_2 (
    .in0(ALU_out), .in1(Sp), .out(multiplexer_2_out), .sel(stack_flag));
  Multiplexer #(.width(16), .enable("false")) multiplexer_3 (
    .in0(read_addr), .in1(write_addr), .out(multiplexer_3_out), .sel(write_RAM));
  RAM_Reader ram_reader_2 (
    .Instruction_Address(multiplexer_2_out), .Enable(read_RAM), .Clock(CLK), .Clear(Reset),
    .Read_time(Read_Time), .Address(read_addr), .Ram_Data(Ram_Data), .Dead_time(DT_Reader),
    .Chip_Select(CS_reader), .RAM_O1(RAM_Out_0), .RAM_O2(RAM_Out_1), .RAM_O3(RAM_Out_2), .RAM_O4(RAM_Out_3));
  Multiplexer #(.width(16), .enable("false")) multiplexer_4 (
    .in0(multiplexer_3_out), .in1(im_addr), .out(Address), .sel(IM_Chip_Select));
  Multiplexer #(.width(32), .enable("false")) multiplexer_5 (
    .in0(ALU_out), .in1(Sp), .out(multiplexer_5_out), .sel(stack_flag));
  or or_7 (or_7_out, DT_Reader, DT_Writer);
  Multiplexer #(.width(32), .enable("false")) multiplexer_6 (
    .in0(kbd_data32), .in1({32{1'b1}}), .out(multiplexer_6_out), .sel(minus_1));
  Random #(.width(32)) random_1 (.clk(CLK), .next(En_rnd), .out(random_1_out));  // open: clr
  Multiplexer #(.width(32), .enable("false")) multiplexer_7 (
    .in0(Rt_t), .in1({Rs_t, TTY_ASCII_Data}), .out(multiplexer_7_out), .sel(push));
  RAM_Writer ram_writer_1 (
    .Enable(write_RAM), .Clock(CLK), .Clear(Reset), .Read_time(Write_Time),
    .Instruction_Address(multiplexer_5_out), .RAM_I1(RAM_In_0), .RAM_I2(RAM_In_1), .RAM_I3(RAM_In_2),
    .Bank_Mask(Mask), .RAM_I4(RAM_In_3), .Address(write_addr), .Dead_time(DT_Writer),
    .Chip_Select(nRead_Write), .Data(multiplexer_7_out));
  Multiplexer #(.select(2), .width(32), .enable("false")) multiplexer_8 (
    .in0(Hi), .in1(Lo), .in2(multiplexer_6_out), .in3(random_1_out), .out(multiplexer_8_out),
    .sel(Rf_in_select));
  Control_Unit control_unit_1 (
    .in_1(nop), .out_40(read_RAM), .in_2(mulu), .out_41(write_RAM), .in_3(sltu), .out_42(write_RF),
    .in_4(\xor ), .in_5(pop), .out_43(TTY_Enable), .in_6(jr), .out_44(Kbd_Enable), .in_7(halt), .in_8(addi),
    .out_45(Stop), .in_9(ori), .out_46(Next), .in_10(beq), .in_11(bltz), .in_12(jump), .in_13(add),
    .in_14(div), .ALU_flag(ALU_flag), .in_15(\and ), .ALU_op(ALU_selector), .in_16(push), .ALU_sign(Sign),
    .in_17(mfhi), .in_18(tty), .stack_flag(stack_flag), .in_19(slti), .pop_push_flag(push_pop), .in_20(xori),
    .in_21(bne), .in_22(sub), .in_23(divu), .in_31(instr_loaded), .in_24(\or ), .in_33(or_7_out),
    .in_25(mflo), .in_26(rnd), .in_36(CLK), .in_27(sltiu), .in_28(lw), .in_29(blez), .in_30(mult),
    .in_32(slt), .in_34(\nor ), .in_35(kbd), .in_37(andi), .in_38(sw), .in_39(bgtz), .enable_pop(pop_enable),
    .enable_push(push_enable), .out_54(En_Cu), .out_55(En_rnd));
  Multiplexer #(.width(32), .enable("false")) multiplexer_9 (
    .in0(ALU_out), .in1(multiplexer_8_out), .out(multiplexer_9_out), .sel(this_op));
  not not_1 (not_1_out, HiLo_Type);
  Register #(.width(32), .trigger("high")) register_1 (
    .D(multiplexer_9_out), .en(not_1_out), .Q(register_1_q), .clk(1'b1), .clr(Reset));
  Priority_Encoder #(.select(2)) priority_encoder_1 (
    .in0(mfhi), .in1(mflo), .in2(kbd), .in3(rnd), .out(Rf_in_select));  // open: gs, en_out, en_in
  or or_8 (this_op, mfhi, mflo, kbd, rnd);
  Multiplexer #(.width(32), .enable("false")) multiplexer_10 (
    .in0(register_1_q), .in1(Ram_Data), .out(multiplexer_10_out), .sel(RAM_R_Type));
  Multiplexer #(.width(32), .enable("false")) multiplexer_11 (
    .in0(Rt_t), .in1(extended_imm), .out(multiplexer_11_out), .sel(I_Type));
  Multiplexer #(.width(5), .enable("false")) multiplexer_12 (
    .in0(Rd), .in1(Rt), .out(multiplexer_12_out), .sel(I_Type));
  and and_7 (and_7_out, stack_flag, write_RF);
  Register_File register_file_1 (
    .Out1_Selector(Rs), .Input(multiplexer_10_out), .Out2_Selector(Rt), .Get1({Rs_t, TTY_ASCII_Data}),
    .Get2(Rt_t), .In_Selector(multiplexer_12_out), .Clock(CLK), .Reset(Reset), .Hi_Lo_Write(HiLo_Type),
    .Stack_Instruction({stack_flag, push_pop}), .Read_Write(write_RF), .Hi_In(remainder), .Lo_In(ALU_out),
    .Hi_Out(Hi), .lo_Out(Lo), .Sp_Out(Sp), .Stack_r_w(and_7_out));
  ALU alu_1 (
    .Selector(ALU_selector), .In1({Rs_t, TTY_ASCII_Data}), .In2(multiplexer_11_out), .Output(ALU_out),
    .ZF(alu_1_zf), .Carry(alu_1_carry), .SF(alu_1_sf), .Remainder(remainder), .in_4(Sign));
  // Probe on ALU_out
  or or_9 (or_9_out, mult, mulu, div, divu);
  or or_10 (RAM_R_Type, lw, pop);
  or or_11 (I_Type, lw, addi, slti, sltiu, andi, ori, xori, sw);
  and and_8 (HiLo_Type, or_9_out, write_RF);

  assign Kbd_Clear = Reset;

  // Other names for the same wires on the sheet: CS = Chip_Select; KBD_AVAIL = Kbd_Available; CLR = Reset;
  //   KBD_CLR = Reset; KBD_DATA[6:0] = Kbd_ASCII_Data; RAM_A[15:0] = Address; RAM_INPUT_0[31:0] = RAM_In_0;
  //   RAM_INPUT_1[31:0] = RAM_In_1; RAM_INPUT_2[31:0] = RAM_In_2; RAM_INPUT_3[31:0] = RAM_In_3; RAM_MASK[3:0] = Mask;
  //   RAM_OUTPUT_0[31:0] = RAM_Out_0; RAM_OUTPUT_1[31:0] = RAM_Out_1; RAM_OUTPUT_2[31:0] = RAM_Out_2;
  //   RAM_OUTPUT_3[31:0] = RAM_Out_3; Rs_t[6:0] = TTY_ASCII_Data; TTY_DATA[6:0] = TTY_ASCII_Data;
  //   CS_writer = nRead_Write; RW = nRead_Write

  // Notes on the sheet:
  //   RAM ADDRESS
  //   DATA FROM RAM
  //   DATA TO RAM
  //   DATA WRITE MASK
  //   RAM TIMING
  //   RAM CONTROL
  //   KEYBOARD
  //   TTY
  //   SEQUENCING
  //   INSTRUCTION MEMORY
  //   out is LOW
endmodule

module RAM_Dispatcher (
  input  [3:0] WriteTime,
  input  Clock,
  input  CLR,
  output [31:0] Data,
  output [15:0] Address,
  output [3:0] Mask,
  output Finished,
  output Write
);

  wire demultiplexer_2_out1, demultiplexer_3_out1, End, IDLE_q, IncAddr, Load, or_1_out, or_2_out, While_q,
       WriteEnd;
  wire [3:0] counter_1_q;
  wire [31:0] CurrentAddress_q;

  Counter #(.width(32), .max('hffffffff)) CurrentAddress (
    .count(IncAddr), .Q({CurrentAddress_q[31:18], Address, CurrentAddress_q[1:0]}), .clk(Clock), .clr(CLR));  // open: load, D, carry
  or or_1 (or_1_out, IncAddr, demultiplexer_3_out1, Finished);
  D_Flip_Flop IDLE (.clk(Clock), .D(or_1_out), .Q(IDLE_q), .preset(CLR));  // open: Qn, en, reset
  Demultiplexer #(.enable("false")) demultiplexer_1 (.out0(Load), .out1(Finished), .in(IDLE_q), .sel(End));
  D_Flip_Flop While (.clk(Clock), .D(or_2_out), .Q(While_q), .reset(CLR));  // open: Qn, preset, en
  or or_2 (or_2_out, Write, Load);
  RAM_part #(.addrWidth(18), .dataWidth(32)) ram_1 (
    .addr({Address, CurrentAddress_q[1:0]}), .data(Data), .clk(Clock));  // open: sel, ld, clr
  Demultiplexer #(.enable("false")) demultiplexer_2 (
    .out0(Write), .out1(demultiplexer_2_out1), .in(While_q), .sel(WriteEnd));
  Decoder #(.select(2)) decoder_1 (
    .out0(Mask[0]), .out1(Mask[1]), .out2(Mask[2]), .out3(Mask[3]), .sel(CurrentAddress_q[1:0]));  // open: en
  Demultiplexer #(.enable("false")) demultiplexer_3 (
    .out0(IncAddr), .out1(demultiplexer_3_out1), .in(demultiplexer_2_out1), .sel(End));
  Counter #(.width(4), .max('hf)) counter_1 (
    .load(Load), .D(WriteTime), .count(Write), .Q(counter_1_q), .clk(Clock));  // open: carry, clr
  Comparator #(.width(32)) comparator_1 (.a(Data), .b({32{1'b1}}), .eq(End));  // open: gt, lt
  Comparator #(.width(4)) comparator_2 (.a(4'b0000), .b(counter_1_q), .eq(WriteEnd));  // open: gt, lt

  // Other names for the same wires on the sheet: CLK = Clock; Count = Write; WT[3:0] = WriteTime
endmodule
